# Fritzing sketch wiring-sketch (saved by Fritzing 0.9.10b)
breadboards: 1

parts:
  Part1 = Arduino Mega 2560 (Rev3)
  Part2 = EasyDriver_v44
  M2 = Stepper Motor - Bipolar
  J1 = Power Jack [package=power_jack_slot]
  LED1 = smd LED [color="Blue (430nm)" package="0603 [SMD]"]
  LED2 = smd LED [color="Blue (430nm)" package="0603 [SMD]"]
  LED3 = smd LED [color="Blue (430nm)" package="0603 [SMD]"]
  LED4 = smd LED [color="Blue (430nm)" package="0603 [SMD]"]
  LED5 = smd LED [color="Blue (430nm)" package="0603 [SMD]"]
  LED6 = smd LED [color="Blue (430nm)" package="0603 [SMD]"]
  LED7 = smd LED [color="Blue (430nm)" package="0603 [SMD]"]
  LED8 = smd LED [color="Blue (430nm)" package="0603 [SMD]"]
  LED9 = smd LED [color="Blue (430nm)" package="0603 [SMD]"]
  LED10 = smd LED [color="Blue (430nm)" package="0603 [SMD]"]
  LED11 = smd LED [color="Blue (430nm)" package="0603 [SMD]"]
  LED12 = smd LED [color="Blue (430nm)" package="0603 [SMD]"]
  LED13 = smd LED [color="Blue (430nm)" package="0603 [SMD]"]
  LED14 = smd LED [color="Blue (430nm)" package="0603 [SMD]"]
  S1 = Round Pushbutton
  R1 = Resistor [tolerance=±5% resistance=220 package="1206 [SMD]"]
  J2 = Basic Servo

nets:
  N1: Part1.A8, LED1.anode
  N2: Part1.A9, LED3.anode
  N3: Part1.A10, LED5.anode
  N4: Part1.A11, LED7.anode
  N5: Part1.A12, LED9.anode
  N6: Part1.A13, LED11.anode
  N7: Part1.A14, LED13.anode
  N8: Part1.A0, S1.leg0, R1.Pin_1
  N9: Part1.D10_PWM, J2.pulse
  N10: Part1.D9_PWM, Part2.DIR
  N11: Part1.D8_PWM, Part2.STEP
  5V: Part1.5V, Part2.VCC, LED2.anode, LED4.anode, LED6.anode, LED8.anode, LED10.anode, LED12.anode, LED14.anode, R1.Pin_0
  GND: Part1.GND, Part2.GND, J1.PWR, LED1.cathode, LED2.cathode, LED3.cathode, LED4.cathode, LED5.cathode, LED6.cathode, LED7.cathode, LED8.cathode, LED9.cathode, LED10.cathode, LED11.cathode, LED12.cathode, LED13.cathode, LED14.cathode, S1.leg1
  N12: Part2.V+, J1.GNDBREAK, J1.GND
  N13: Part2.OUT2A, M2.A
  N14: Part2.OUT2B, M2.C
  N15: Part2.OUT1A, M2.B
  N16: Part2.OUT1B, M2.D

notes:
  LIMIT Switch
  9V DC in
  Dropper servo
